# Fritzing sketch Hall Effect Sensor pcb (saved by Fritzing 0.9.3b)
circuit board: 4.33572cm x 2.46168cm
breadboards: 1

parts:
  Raspberry_Pi = male pin header, 6 pins [form="♂ (male)"]
  Hall_effect_sensor = male pin header, 3 pins [form="♂ (male)"]

nets:
  N1: Raspberry_Pi.pin1, Hall_effect_sensor.pin1
  N2: Raspberry_Pi.pin5, Hall_effect_sensor.pin2
  N3: Raspberry_Pi.pin6, Hall_effect_sensor.pin3

notes:
  Vcc 5V
  SIG - GPIO18
  GND
  Seung Min Song
