# Fritzing sketch Hall Effect Sensor (saved by Fritzing 0.9.3b)
circuit board: 3.69711cm x 2.11666cm
breadboards: 1

parts:
  Raspberry_Pi = Raspberry Pi B+
  Hall_Effect_Sensor = HALL-EFFECT [package=sc70]

nets:
  GND: Raspberry_Pi.GND, Hall_Effect_Sensor.GND
  N1: Raspberry_Pi.GPIO18, Hall_Effect_Sensor.OUT
  5V: Raspberry_Pi.5V, Hall_Effect_Sensor.VCC

notes:
  Seung Min Song

// code stored in the sketch: Hall Effect Sensor Bread board.ino

